// Logisim project processor.circ as structural Verilog: 7 circuits, main circuit main
module main (
  input  [31:0] Instruction,
  input  WrEn,
  input  [1:0] in_3,
  input  [31:0] LOAD_DATA1,
  output [31:0] out_5
);

  wire clock_1_out, comparator_1_eq, comparator_2_eq, DATA_SELECTOR;
  wire [2:0] FUNCT3;
  wire [3:0] decode_1_out_2;
  wire [4:0] RD, RS1, RS2;
  wire [6:0] FUNCT7, OPCODE, register_4_q;
  wire [31:0] alu_1_out_4, multiplexer_1_out, register_1_q, register_5_q, register_6_q, RS1_Input, RS2_Input;

  Clock clock_1 (.out(clock_1_out));
  Register #(.width(32)) register_1 (.D(Instruction), .Q(register_1_q), .clk(clock_1_out));  // open: en, clr
  IF if_1 (
    .Instruction(register_1_q), .in_2(in_3), .OPCODE(OPCODE), .RD(RD), .FUNCT3(FUNCT3), .RS1(RS1), .RS2(RS2),
    .FUNCT7(FUNCT7));
  Register #(.width(7)) register_2 (.D(OPCODE), .clk(clock_1_out));  // open: en, Q, clr
  Register #(.width(3)) register_3 (.D(FUNCT3), .clk(clock_1_out));  // open: en, Q, clr
  Register #(.width(7)) register_4 (.D(FUNCT7), .Q(register_4_q), .clk(clock_1_out));  // open: en, clr
  Register #(.width(32)) register_5 (.D(LOAD_DATA1), .Q(register_5_q), .clk(clock_1_out));  // open: en, clr
  Decode decode_1 (.in_1(register_4_q), .out_2(decode_1_out_2));
  Comparator #(.width(5)) comparator_1 (.a(RS2), .b({5{1'b0}}), .eq(comparator_1_eq));  // open: gt, lt
  Comparator #(.width(5)) comparator_2 (.a(RS1), .b({5{1'b0}}), .eq(comparator_2_eq));  // open: gt, lt
  // Probe on multiplexer_1_out
  Multiplexer #(.width(32)) multiplexer_1 (
    .in0(register_6_q), .in1(register_5_q), .out(multiplexer_1_out), .sel(DATA_SELECTOR));  // open: en
  Register_File register_file_1 (
    .Write_Data(multiplexer_1_out), .RS1(RS1), .RS2(RS2), .RD(RD), .WrEn(1'b1), .clk(clock_1_out),
    .RS1_2(RS1_Input), .RS2_2(RS2_Input));  // open: RD_2
  ALU alu_1 (.RS1(RS1_Input), .RS2(RS2_Input), .SELECTOR(decode_1_out_2), .out_4(alu_1_out_4));
  or or_1 (DATA_SELECTOR, comparator_1_eq, comparator_2_eq);
  // Probe on RS1_Input
  Register #(.width(32)) register_6 (.D(alu_1_out_4), .Q(register_6_q), .clk(clock_1_out));  // open: en, clr
  // Probe on RS2_Input
  MEM mem_1 (.Address(RD), .Write_Data(multiplexer_1_out), .WriteEn(WrEn), .clk(clock_1_out), .Read_Data(out_5));

  // Other names for the same wires on the sheet: R_I_J_TYPE[1:0] = in_3
endmodule

// Arithmetic Logic Unit
module ALU (
  input  [31:0] RS1,
  input  [31:0] RS2,
  input  [3:0] SELECTOR,
  output [31:0] out_4
);

  wire comparator_1_eq, comparator_1_gt, comparator_1_lt;
  wire [31:0] adder_1_out, and_1_out, bit_extender_1_out, bit_extender_2_out, bit_extender_3_out,
       divider_1_out, multiplier_1_out, or_1_out, shifter_1_out, shifter_2_out, shifter_3_out,
       subtractor_1_out, xor_1_out;

  Adder #(.width(32)) adder_1 (.a(RS1), .b(RS2), .out(adder_1_out));  // open: cin, cout
  Subtractor #(.width(32)) subtractor_1 (.a(RS1), .b(RS2), .out(subtractor_1_out));  // open: bin, bout
  Multiplier #(.width(32)) multiplier_1 (.a(RS1), .b(RS2), .out(multiplier_1_out));  // open: cin, cout
  Divider #(.width(32)) divider_1 (.a(RS1), .b(RS2), .out(divider_1_out));  // open: upper, rem
  assign and_1_out = RS1 & RS2;  // AND_Gate and_1, 32 bits wide
  assign xor_1_out = RS1 ^ RS2;  // XOR_Gate xor_1, 32 bits wide
  assign or_1_out = RS1 | RS2;  // OR_Gate or_1, 32 bits wide
  Comparator #(.width(32)) comparator_1 (
    .a(RS1), .b(RS2), .gt(comparator_1_gt), .eq(comparator_1_eq), .lt(comparator_1_lt));
  Shifter #(.width(32)) shifter_1 (.in(RS1), .\dist (RS2[4:0]), .out(shifter_1_out));
  Shifter #(.width(32)) shifter_2 (.in(RS1), .\dist (RS2[4:0]), .out(shifter_2_out));
  Shifter #(.width(32), .shift("ar")) shifter_3 (.in(RS1), .\dist (RS2[4:0]), .out(shifter_3_out));
  assign bit_extender_1_out = {{31{1'b0}}, comparator_1_gt};  // Bit_Extender bit_extender_1
  assign bit_extender_2_out = {{31{1'b0}}, comparator_1_eq};  // Bit_Extender bit_extender_2
  assign bit_extender_3_out = {{31{1'b0}}, comparator_1_lt};  // Bit_Extender bit_extender_3
  Multiplexer #(.select(4), .width(32)) multiplexer_1 (
    .in0(adder_1_out), .in1(subtractor_1_out), .in2(multiplier_1_out), .in3(divider_1_out), .in4(and_1_out),
    .in5(xor_1_out), .in6(or_1_out), .in7(bit_extender_1_out), .in8(bit_extender_2_out),
    .in9(bit_extender_3_out), .in10(shifter_1_out), .in11(shifter_2_out), .in12(shifter_3_out), .in13(RS2),
    .out(out_4), .sel(SELECTOR));  // open: in14, in15, en

  // Other names for the same wires on the sheet: bsel[31:0] = RS2
endmodule

module Decode (
  input  [6:0] in_1,
  output [3:0] out_2
);

  Bit_Extender #(.in_width(7), .out_width(4)) bit_extender_1 (.in(in_1), .out(out_2));

  // Other names for the same wires on the sheet: Funct7_ID[6:0] = in_1
endmodule

module IF (
  input  [31:0] Instruction,
  input  [1:0] in_2,
  output [6:0] OPCODE,
  output [4:0] RD,
  output [2:0] FUNCT3,
  output [4:0] RS1,
  output [4:0] RS2,
  output [6:0] FUNCT7
);

  Multiplexer #(.select(2), .width(7)) multiplexer_1 (
    .in0(Instruction[6:0]), .out(OPCODE), .sel(in_2));  // open: in1, in2, in3, en
  Multiplexer #(.select(2), .width(5)) multiplexer_2 (
    .in0(Instruction[11:7]), .out(RD), .sel(in_2));  // open: in1, in2, in3, en
  Multiplexer #(.select(2), .width(3)) multiplexer_3 (
    .in0(Instruction[14:12]), .out(FUNCT3), .sel(in_2));  // open: in1, in2, in3, en
  Multiplexer #(.select(2), .width(5)) multiplexer_4 (
    .in0(Instruction[19:15]), .out(RS1), .sel(in_2));  // open: in1, in2, in3, en
  Multiplexer #(.select(2), .width(5)) multiplexer_5 (
    .in0(Instruction[24:20]), .out(RS2), .sel(in_2));  // open: in1, in2, in3, en
  Multiplexer #(.select(2), .width(7)) multiplexer_6 (
    .in0(Instruction[31:25]), .out(FUNCT7), .sel(in_2));  // open: in1, in2, in3, en
  // Probe on nothing
endmodule

module Register_File (
  input  [31:0] Write_Data,
  input  [4:0] RS1,
  input  [4:0] RS2,
  input  [4:0] RD,
  input  WrEn,
  input  clk,
  output [31:0] RS1_2,
  output [31:0] RS2_2,
  output [31:0] RD_2
);

  wire R0_En, R1_En, R2_En, R3_En, R4_En, R5_En, R6_En, R7_En;
  wire [31:0] R0, R1, R2, R3, R4, R5, R6, R7;

  Demultiplexer #(.select(5)) demultiplexer_1 (
    .out0(R0_En), .out1(R1_En), .out2(R2_En), .out3(R3_En), .out4(R4_En), .out5(R5_En), .out6(R6_En),
    .out7(R7_En), .in(WrEn), .sel(RD));  // open: out8, out9, out10, out11, out12, out13, out14, out15, out16, out17, out18, out19, out20, out21, out22, out23, out24, out25, out26, out27, out28, out29, out30, out31, en
  Register #(.width(32)) u_R0 (.D({32{1'b0}}), .en(R0_En), .Q(R0), .clk(clk));  // open: clr
  Register #(.width(32)) u_R1 (.D(Write_Data), .en(R1_En), .Q(R1), .clk(clk));  // open: clr
  Register #(.width(32)) u_R2 (.D(Write_Data), .en(R2_En), .Q(R2), .clk(clk));  // open: clr
  Register #(.width(32)) u_R3 (.D(Write_Data), .en(R3_En), .Q(R3), .clk(clk));  // open: clr
  Register #(.width(32)) u_R4 (.D(Write_Data), .en(R4_En), .Q(R4), .clk(clk));  // open: clr
  Register #(.width(32)) u_R5 (.D(Write_Data), .en(R5_En), .Q(R5), .clk(clk));  // open: clr
  Register #(.width(32)) u_R6 (.D(Write_Data), .en(R6_En), .Q(R6), .clk(clk));  // open: clr
  Register #(.width(32)) u_R7 (.D(Write_Data), .en(R7_En), .Q(R7), .clk(clk));  // open: clr
  Multiplexer #(.select(5), .width(32)) multiplexer_1 (
    .in0(R0), .in1(R1), .in2(R2), .in3(R3), .in4(R4), .in5(R5), .in6(R6), .in7(R7), .out(RS1_2), .sel(RS1));  // open: in8, in9, in10, in11, in12, in13, in14, in15, in16, in17, in18, in19, in20, in21, in22, in23, in24, in25, in26, in27, in28, in29, in30, in31, en
  Multiplexer #(.select(5), .width(32)) multiplexer_2 (
    .in0(R0), .in1(R1), .in2(R2), .in3(R3), .in4(R4), .in5(R5), .in6(R6), .in7(R7), .out(RS2_2), .sel(RS2));  // open: in8, in9, in10, in11, in12, in13, in14, in15, in16, in17, in18, in19, in20, in21, in22, in23, in24, in25, in26, in27, in28, in29, in30, in31, en
  Multiplexer #(.select(5), .width(32)) multiplexer_3 (
    .in0(R0), .in1(R1), .in2(R2), .in3(R3), .in4(R4), .in5(R5), .in6(R6), .in7(R7), .out(RD_2), .sel(RD));  // open: in8, in9, in10, in11, in12, in13, in14, in15, in16, in17, in18, in19, in20, in21, in22, in23, in24, in25, in26, in27, in28, in29, in30, in31, en
endmodule

module Control (
  input  [31:0] Instruction,
  input  BRLT,
  input  BREQ,
  output A_Sel,
  output B_Sel,
  output MemRW,
  output RWEn,
  output PC_Sel
);

  wire and_1_out, branch, comparator_1_eq, comparator_2_eq, comparator_3_eq, comparator_5_eq,
       comparator_6_eq, comparator_7_eq, comparator_8_eq;

  or or_1 (branch, BRLT, BREQ);
  Comparator #(.width(7)) comparator_1 (.a(Instruction[6:0]), .b(7'b0110011), .eq(comparator_1_eq));  // open: gt, lt
  Comparator #(.width(7)) comparator_2 (.a(Instruction[6:0]), .b(7'b0000011), .eq(comparator_2_eq));  // open: gt, lt
  Comparator #(.width(7)) comparator_3 (.a(Instruction[6:0]), .b(7'b0010011), .eq(comparator_3_eq));  // open: gt, lt
  Comparator #(.width(7)) comparator_4 (.a(Instruction[6:0]), .b(7'b0100011), .eq(MemRW));  // open: gt, lt
  Comparator #(.width(7)) comparator_5 (.a(Instruction[6:0]), .b(7'b0110111), .eq(comparator_5_eq));  // open: gt, lt
  Comparator #(.width(7)) comparator_6 (.a(Instruction[6:0]), .b(7'b1100011), .eq(comparator_6_eq));  // open: gt, lt
  Comparator #(.width(7)) comparator_7 (.a(Instruction[6:0]), .b(7'b1101111), .eq(comparator_7_eq));  // open: gt, lt
  Comparator #(.width(7)) comparator_8 (.a(Instruction[6:0]), .b(7'b1100111), .eq(comparator_8_eq));  // open: gt, lt
  and and_1 (and_1_out, branch, comparator_6_eq);
  or or_2 (A_Sel, comparator_1_eq, comparator_2_eq, comparator_3_eq, MemRW, comparator_8_eq);
  or or_3 (B_Sel, comparator_2_eq, comparator_3_eq, comparator_5_eq, comparator_6_eq, comparator_7_eq, comparator_8_eq);
  or or_4 (RWEn, MemRW, comparator_6_eq);
  or or_5 (PC_Sel, and_1_out, comparator_7_eq, comparator_8_eq);

  // Other names for the same wires on the sheet: Opcode[6:0] = Instruction[6:0]; Funct3[2:0] = Instruction[14:12]
endmodule

module MEM (
  input  [4:0] Address,
  input  [31:0] Write_Data,
  input  WriteEn,
  input  clk,
  output [31:0] Read_Data
);

  wire and_1_out;

  buf and_1 (and_1_out, clk);  // AND_Gate
  RAM #(.addrWidth(5), .dataWidth(32), .bus("separate")) ram_1 (
    .addr(Address), .din(Write_Data), .data(Read_Data), .str(WriteEn), .sel(1'b1), .clk(and_1_out), .ld(1'b1));  // open: clr
endmodule
